// Logisim project 2207111 Alu with Booth's multiplier.circ as structural Verilog: 29 circuits, main circuit MINI COMP
// OR
module _20_bit_OR (
  input  [19:0] in_1,
  input  [19:0] in_2,
  output [19:0] out_3
);

  assign out_3 = in_1 | in_2;  // OR_Gate or_1, 20 bits wide

  // Notes on the sheet:
  //   A
  //   B
  //   2207111
  //   A+B
endmodule

// AND
module _20_bit_AND (
  input  [19:0] in_1,
  input  [19:0] in_2,
  output [19:0] out_3
);

  assign out_3 = in_1 & in_2;  // AND_Gate and_1, 20 bits wide

  // Notes on the sheet:
  //   A
  //   B
  //   2207111
  //   A.B
endmodule

module Zero_Detector (
  input  [19:0] Output,
  output ZERO
);

  wire or_1_out;

  or or_1 (or_1_out, Output[0], Output[1], Output[2], Output[3], Output[4], Output[5], Output[6], Output[7], Output[8], Output[9], Output[10], Output[11], Output[12], Output[13], Output[14], Output[15], Output[16], Output[17], Output[18], Output[19]);
  not not_1 (ZERO, or_1_out);

  // Notes on the sheet:
  //   2207111
endmodule

module NEG_Detector (
  input  [19:0] in_1,
  output out_2
);


  assign out_2 = in_1[19];

  // Notes on the sheet:
  //   2207111
endmodule

module Carry_generator (
  input  Cin,
  input  G0,
  input  P0,
  input  G1,
  input  P1,
  input  G2,
  input  P2,
  input  G3,
  input  P3,
  output C0,
  output C1,
  output C2,
  output C4
);

  wire and_1_out, and_2_out, and_3_out, and_4_out, and_5_out, and_6_out, and_7_out, and_8_out, and_9_out,
       and_10_out;

  and and_1 (and_1_out, G0, P1);
  and and_2 (and_2_out, P2, G1, P3);
  and and_3 (and_3_out, P3, G2);
  and and_4 (and_4_out, Cin, P0);
  and and_5 (and_5_out, Cin, P0, P1);
  and and_6 (and_6_out, G0, P1, P2);
  and and_7 (and_7_out, G1, P2);
  and and_8 (and_8_out, P2, P1, P0, Cin);
  and and_9 (and_9_out, G0, P1, P2, P3);
  and and_10 (and_10_out, P3, P2, P1, P0, Cin);
  or or_1 (C0, and_4_out, G0);
  or or_2 (C1, and_5_out, and_1_out, G1);
  or or_3 (C2, G2, and_6_out, and_7_out, and_8_out);
  or or_4 (C4, G3, and_9_out, and_2_out, and_10_out, and_3_out);

  // Notes on the sheet:
  //   2207111
endmodule

// A/S
module _20_bit_adder_subtractor (
  input  Cin,
  input  [19:0] in_2,
  input  [19:0] in_3,
  output [19:0] Sum_sub,
  output Cout,
  output OVR
);

  wire n4_bit_cla_1_c4, n4_bit_cla_2_c4, n4_bit_cla_3_c4, n4_bit_cla_4_c4;
  wire [19:0] bit_extender_1_out, xor_1_out;

  assign bit_extender_1_out = {{19{Cin}}, Cin};  // Bit_Extender bit_extender_1
  assign xor_1_out = bit_extender_1_out ^ in_3;  // XOR_Gate xor_1, 20 bits wide
  _4_bit_CLA u_4_bit_cla_1 (
    .cin(Cin), .A(in_2[3:0]), .B(xor_1_out[3:0]), .C4(n4_bit_cla_1_c4), .S(Sum_sub[3:0]));  // open: C3
  _4_bit_CLA u_4_bit_cla_2 (
    .cin(n4_bit_cla_1_c4), .A(in_2[7:4]), .B(xor_1_out[7:4]), .C4(n4_bit_cla_2_c4), .S(Sum_sub[7:4]));  // open: C3
  _4_bit_CLA u_4_bit_cla_3 (
    .cin(n4_bit_cla_2_c4), .A(in_2[11:8]), .B(xor_1_out[11:8]), .C4(n4_bit_cla_3_c4), .S(Sum_sub[11:8]));  // open: C3
  _4_bit_CLA u_4_bit_cla_4 (
    .cin(n4_bit_cla_3_c4), .A(in_2[15:12]), .B(xor_1_out[15:12]), .C4(n4_bit_cla_4_c4), .S(Sum_sub[15:12]));  // open: C3
  _4_bit_CLA u_4_bit_cla_5 (
    .cin(n4_bit_cla_4_c4), .A(in_2[19:16]), .B(xor_1_out[19:16]), .C4(Cout), .S(Sum_sub[19:16]));  // open: C3
  xor xor_2 (OVR, Cout, n4_bit_cla_4_c4);

  // Notes on the sheet:
  //   2207111
endmodule

// 4BAS
module _4_bit_CLA (
  input  cin,
  input  [3:0] A,
  input  [3:0] B,
  output C3,
  output C4,
  output [3:0] S
);

  wire carry_generator_1_c0, carry_generator_1_c1;
  wire [3:0] G_out, P_out;

  assign G_out = A & B;  // AND_Gate G, 4 bits wide
  assign P_out = A ^ B;  // XOR_Gate P, 4 bits wide
  Carry_generator carry_generator_1 (
    .Cin(cin), .G0(G_out[0]), .P0(P_out[0]), .G1(G_out[1]), .P1(P_out[1]), .G2(G_out[2]), .P2(P_out[2]),
    .G3(G_out[3]), .P3(P_out[3]), .C0(carry_generator_1_c0), .C1(carry_generator_1_c1), .C2(C3), .C4(C4));
  xor S0 (S[0], P_out[0], cin);
  xor S1 (S[1], P_out[1], carry_generator_1_c0);
  xor S2 (S[2], P_out[2], carry_generator_1_c1);
  xor S3 (S[3], P_out[3], C3);

  // Notes on the sheet:
  //   2207111
endmodule

// ALU
module Alu (
  input  [19:0] A,
  input  [19:0] B,
  input  [1:0] C,
  output [19:0] Output,
  output COUT,
  output Overflow,
  output Zero,
  output Negative
);

  wire [19:0] n20_bit_adder_subtractor_1_sum_sub, n20_bit_and_1_out_3, n20_bit_or_1_out_3;

  // Probe on B
  // Probe on A
  _20_bit_AND u_20_bit_and_1 (.in_1(A), .in_2(B), .out_3(n20_bit_and_1_out_3));
  _20_bit_OR u_20_bit_or_1 (.in_1(A), .in_2(B), .out_3(n20_bit_or_1_out_3));
  _20_bit_adder_subtractor u_20_bit_adder_subtractor_1 (
    .Cin(C[0]), .in_2(A), .in_3(B), .Sum_sub(n20_bit_adder_subtractor_1_sum_sub), .Cout(COUT), .OVR(Overflow));
  Multiplexer #(.select(2), .width(20), .enable("false")) multiplexer_1 (
    .in0(n20_bit_and_1_out_3), .in1(n20_bit_or_1_out_3), .in2(n20_bit_adder_subtractor_1_sum_sub),
    .in3(n20_bit_adder_subtractor_1_sum_sub), .out(Output), .sel(C));
  // Probe on Output
  Zero_Detector zero_detector_1 (.Output(Output), .ZERO(Zero));
  NEG_Detector neg_detector_1 (.in_1(Output), .out_2(Negative));

  // Notes on the sheet:
  //   00-AND
  //   01-OR
  //   10-ADD
  //   11-SUB
  //   2207111 ALU
endmodule

module controller (
  input  [1:0] Q,
  input  [2:0] T,
  input  C,
  output DA,
  output DB,
  output DC
);

  wire and_1_out, and_2_out, and_3_out, and_4_out, and_5_out, or_4_out, or_5_out, Q0, Q1, Q2, Q3, T0, T1, T2,
       T3, T4, T5, T6, T7;

  Decoder #(.select(2), .enable("false")) decoder_1 (.out0(Q0), .out1(Q1), .out2(Q2), .out3(Q3), .sel(Q));
  Decoder #(.select(3), .enable("false")) decoder_2 (
    .out0(T0), .out1(T1), .out2(T2), .out3(T3), .out4(T4), .out5(T5), .out6(T6), .out7(T7), .sel(T));
  or or_1 (DA, T0, and_5_out, T3, T4, and_1_out, T7);
  or or_2 (DB, T1, and_2_out, T5, T6, T6, T7);
  or or_3 (DC, T5, and_3_out, T3, T4, and_4_out, T7);
  and and_1 (and_1_out, T6, C);
  and and_2 (and_2_out, T2, Q2);
  and and_3 (and_3_out, T2, or_5_out);
  and and_4 (and_4_out, T6, C);
  and and_5 (and_5_out, T2, or_4_out);
  or or_4 (or_4_out, Q0, Q2, Q3);
  or or_5 (or_5_out, Q0, Q1, Q3);

  // Notes on the sheet:
  //   2207111
endmodule

module sequence_decoder (
  input  Clk,
  input  Reset,
  input  Q0,
  input  Q_1,
  input  [4:0] Count,
  output Cl__A__Q_1,
  output LOad__M__Q__Cnt,
  output Load_A,
  output C0,
  output C1,
  output Shr,
  output Dec_Cnt
);

  wire controller_1_da, controller_1_db, controller_1_dc, nor_1_out, T0, T2, T4, T6, T7;
  wire [2:0] T;

  Decoder #(.select(3), .enable("false")) decoder_1 (
    .out0(T0), .out1(Cl__A__Q_1), .out2(T2), .out3(C0), .out4(T4), .out5(Dec_Cnt), .out6(T6), .out7(T7),
    .sel(T));
  controller controller_1 (
    .Q({Q0, Q_1}), .T(T), .C(nor_1_out), .DA(controller_1_da), .DB(controller_1_db), .DC(controller_1_dc));
  nor nor_1 (nor_1_out, Count[0], Count[1], Count[2], Count[3], Count[4]);
  D_Flip_Flop d_ff_1 (.clk(Clk), .D(controller_1_da), .Q(T[0]), .reset(Reset));  // open: Qn, preset, en
  D_Flip_Flop d_ff_2 (.clk(Clk), .D(controller_1_db), .Q(T[1]), .reset(Reset));  // open: Qn, preset, en
  D_Flip_Flop d_ff_3 (.clk(Clk), .D(controller_1_dc), .Q(T[2]), .reset(Reset));  // open: Qn, preset, en
  or or_1 (Load_A, C0, T4);
  or or_2 (C1, T4, C0);

  assign LOad__M__Q__Cnt = Cl__A__Q_1;
  assign Shr = Dec_Cnt;

  // Other names for the same wires on the sheet: T1 = Cl__A__Q_1; T3 = C0; T5 = Dec_Cnt

  // Notes on the sheet:
  //   2207111
endmodule

module booths_multiplier (
  input  [19:0] M_input,
  input  [19:0] Q_input,
  input  Reset,
  output [19:0] out_4,
  output [19:0] out_5
);

  wire A_out, CLK_out, or_1_out, Q__1_q0, Q_out, sequence_decoder_1_cl__a__q_1, sequence_decoder_1_dec_cnt,
       sequence_decoder_1_load__m__q__cnt, sequence_decoder_1_load_a, sequence_decoder_1_shr;
  wire [1:0] sequence_decoder_1_c0;
  wire [4:0] counter_1_q;
  wire [19:0] alu_1_output, M_q19;

  Clock CLK (.out(CLK_out));
  sequence_decoder sequence_decoder_1 (
    .Clk(CLK_out), .Reset(Reset), .Q0(out_5[0]), .Q_1(Q__1_q0), .Count(counter_1_q),
    .Cl__A__Q_1(sequence_decoder_1_cl__a__q_1), .LOad__M__Q__Cnt(sequence_decoder_1_load__m__q__cnt),
    .Load_A(sequence_decoder_1_load_a), .C0(sequence_decoder_1_c0[0]), .C1(sequence_decoder_1_c0[1]),
    .Shr(sequence_decoder_1_shr), .Dec_Cnt(sequence_decoder_1_dec_cnt));
  or or_1 (or_1_out, sequence_decoder_1_load__m__q__cnt, sequence_decoder_1_dec_cnt);
  // Probe on Q_input
  Shift_Register #(.length(20)) M (
    .shift(1'b0), .clk(CLK_out), .load(sequence_decoder_1_load__m__q__cnt), .d0(M_input[19]), .q0(M_q19[19]),
    .d1(M_input[18]), .q1(M_q19[18]), .d2(M_input[17]), .q2(M_q19[17]), .d3(M_input[16]), .q3(M_q19[16]),
    .d4(M_input[15]), .q4(M_q19[15]), .d5(M_input[14]), .q5(M_q19[14]), .d6(M_input[13]), .q6(M_q19[13]),
    .d7(M_input[12]), .q7(M_q19[12]), .d8(M_input[11]), .q8(M_q19[11]), .d9(M_input[10]), .q9(M_q19[10]),
    .d10(M_input[9]), .q10(M_q19[9]), .d11(M_input[8]), .q11(M_q19[8]), .d12(M_input[7]), .q12(M_q19[7]),
    .d13(M_input[6]), .q13(M_q19[6]), .d14(M_input[5]), .q14(M_q19[5]), .d15(M_input[4]), .q15(M_q19[4]),
    .d16(M_input[3]), .q16(M_q19[3]), .d17(M_input[2]), .q17(M_q19[2]), .d18(M_input[1]), .q18(M_q19[1]),
    .d19(M_input[0]), .q19(M_q19[0]));  // open: in, out, clr
  Counter #(.width(5), .max('h14)) counter_1 (
    .load(or_1_out), .D(5'b10100), .count(sequence_decoder_1_dec_cnt), .Q(counter_1_q), .clk(CLK_out));  // open: carry, clr
  Shift_Register #(.length(20)) A (
    .shift(sequence_decoder_1_shr), .in(out_4[19]), .clk(CLK_out), .out(A_out),
    .load(sequence_decoder_1_load_a), .clr(sequence_decoder_1_cl__a__q_1), .d0(alu_1_output[19]),
    .q0(out_4[19]), .d1(alu_1_output[18]), .q1(out_4[18]), .d2(alu_1_output[17]), .q2(out_4[17]),
    .d3(alu_1_output[16]), .q3(out_4[16]), .d4(alu_1_output[15]), .q4(out_4[15]), .d5(alu_1_output[14]),
    .q5(out_4[14]), .d6(alu_1_output[13]), .q6(out_4[13]), .d7(alu_1_output[12]), .q7(out_4[12]),
    .d8(alu_1_output[11]), .q8(out_4[11]), .d9(alu_1_output[10]), .q9(out_4[10]), .d10(alu_1_output[9]),
    .q10(out_4[9]), .d11(alu_1_output[8]), .q11(out_4[8]), .d12(alu_1_output[7]), .q12(out_4[7]),
    .d13(alu_1_output[6]), .q13(out_4[6]), .d14(alu_1_output[5]), .q14(out_4[5]), .d15(alu_1_output[4]),
    .q15(out_4[4]), .d16(alu_1_output[3]), .q16(out_4[3]), .d17(alu_1_output[2]), .q17(out_4[2]),
    .d18(alu_1_output[1]), .q18(out_4[1]), .d19(alu_1_output[0]), .q19(out_4[0]));
  Alu alu_1 (
    .A(out_4), .B(M_q19), .C(sequence_decoder_1_c0), .Output(alu_1_output));  // open: COUT, Overflow, Zero, Negative
  // Probe on M_input
  // Probe on out_4
  // Probe on out_5
  Shift_Register #(.length(20)) Q (
    .shift(sequence_decoder_1_shr), .in(A_out), .clk(CLK_out), .out(Q_out),
    .load(sequence_decoder_1_load__m__q__cnt), .d0(Q_input[19]), .q0(out_5[19]), .d1(Q_input[18]),
    .q1(out_5[18]), .d2(Q_input[17]), .q2(out_5[17]), .d3(Q_input[16]), .q3(out_5[16]), .d4(Q_input[15]),
    .q4(out_5[15]), .d5(Q_input[14]), .q5(out_5[14]), .d6(Q_input[13]), .q6(out_5[13]), .d7(Q_input[12]),
    .q7(out_5[12]), .d8(Q_input[11]), .q8(out_5[11]), .d9(Q_input[10]), .q9(out_5[10]), .d10(Q_input[9]),
    .q10(out_5[9]), .d11(Q_input[8]), .q11(out_5[8]), .d12(Q_input[7]), .q12(out_5[7]), .d13(Q_input[6]),
    .q13(out_5[6]), .d14(Q_input[5]), .q14(out_5[5]), .d15(Q_input[4]), .q15(out_5[4]), .d16(Q_input[3]),
    .q16(out_5[3]), .d17(Q_input[2]), .q17(out_5[2]), .d18(Q_input[1]), .q18(out_5[1]), .d19(Q_input[0]),
    .q19(out_5[0]));  // open: clr
  Shift_Register #(.length(1)) Q__1 (
    .shift(sequence_decoder_1_shr), .in(Q_out), .clk(CLK_out), .q0(Q__1_q0));  // open: out, load, clr, d0

  // Notes on the sheet:
  //   2207111 Booth's Multiplier
endmodule

// 4PLR
module _4_Bit_PLR (
  input  LOAD,
  input  [3:0] in_2,
  input  CLOCK,
  input  CLEAR,
  output [3:0] out_5
);

  wire and_1_out, and_2_out, and_3_out, and_4_out, and_5_out, and_6_out, and_7_out, and_8_out, not_1_out,
       not_2_out, not_3_out, not_4_out;

  not not_1 (not_1_out, in_2[0]);
  not not_2 (not_2_out, in_2[1]);
  not not_3 (not_3_out, in_2[2]);
  not not_4 (not_4_out, in_2[3]);
  and and_1 (and_1_out, LOAD, in_2[0]);
  and and_2 (and_2_out, LOAD, not_1_out);
  and and_3 (and_3_out, LOAD, in_2[1]);
  and and_4 (and_4_out, LOAD, not_2_out);
  and and_5 (and_5_out, LOAD, in_2[2]);
  and and_6 (and_6_out, LOAD, not_3_out);
  and and_7 (and_7_out, LOAD, in_2[3]);
  and and_8 (and_8_out, LOAD, not_4_out);
  J_K_Flip_Flop j_k_ff_1 (
    .J(and_1_out), .clk(CLOCK), .K(and_2_out), .Q(out_5[0]), .reset(CLEAR));  // open: Qn, preset, en
  J_K_Flip_Flop j_k_ff_2 (
    .J(and_3_out), .clk(CLOCK), .K(and_4_out), .Q(out_5[1]), .reset(CLEAR));  // open: Qn, preset, en
  J_K_Flip_Flop j_k_ff_3 (
    .J(and_5_out), .clk(CLOCK), .K(and_6_out), .Q(out_5[2]), .reset(CLEAR));  // open: Qn, preset, en
  J_K_Flip_Flop j_k_ff_4 (
    .J(and_7_out), .clk(CLOCK), .K(and_8_out), .Q(out_5[3]), .reset(CLEAR));  // open: Qn, preset, en

  // Notes on the sheet:
  //   2207111
endmodule

// 1PLR
module _1_Bit_PLR (
  input  LOAD,
  input  in_2,
  input  CLOCK,
  input  CLEAR,
  output out_5
);

  wire and_1_out, and_2_out, not_1_out;

  not not_1 (not_1_out, in_2);
  and and_1 (and_1_out, LOAD, in_2);
  and and_2 (and_2_out, LOAD, not_1_out);
  J_K_Flip_Flop j_k_ff_1 (.J(and_1_out), .clk(CLOCK), .K(and_2_out), .Q(out_5), .reset(CLEAR));  // open: Qn, preset, en

  // Notes on the sheet:
  //   2207111
endmodule

// 4CPL
module _4_Bit_CPL (
  input  Cin,
  input  Count,
  input  Load,
  input  [3:0] \input ,
  input  Clock,
  input  Clear,
  output [3:0] out_7,
  output Cout
);

  wire and_1_out, and_2_out, and_3_out, and_4_out, and_5_out, and_6_out, and_7_out, and_8_out, and_9_out,
       and_10_out, and_11_out, and_12_out, and_13_out, not_1_out, not_2_out, not_3_out, not_4_out, not_5_out,
       or_1_out, or_2_out, or_3_out, or_4_out, or_5_out, or_6_out, or_7_out, or_8_out;

  not not_1 (not_1_out, Load);
  not not_2 (not_2_out, \input [0]);
  not not_3 (not_3_out, \input [1]);
  not not_4 (not_4_out, \input [2]);
  not not_5 (not_5_out, \input [3]);
  and and_1 (and_1_out, Count, not_1_out);
  and and_2 (and_2_out, Load, \input [0]);
  and and_3 (and_3_out, Load, not_2_out);
  and and_4 (and_4_out, Load, \input [1]);
  and and_5 (and_5_out, Load, not_3_out);
  and and_6 (and_6_out, Load, \input [2]);
  and and_7 (and_7_out, Load, not_4_out);
  and and_8 (and_8_out, Load, \input [3]);
  and and_9 (and_9_out, Load, not_5_out);
  and and_10 (and_10_out, and_1_out, Cin);
  or or_1 (or_1_out, and_2_out, and_10_out);
  or or_2 (or_2_out, and_10_out, and_3_out);
  or or_3 (or_3_out, and_4_out, and_11_out);
  and and_11 (and_11_out, and_1_out, Cin, out_7[0]);
  or or_4 (or_4_out, and_11_out, and_5_out);
  or or_5 (or_5_out, and_6_out, and_12_out);
  and and_12 (and_12_out, out_7[0], Cin, out_7[1], and_1_out);
  or or_6 (or_6_out, and_12_out, and_7_out);
  and and_13 (and_13_out, out_7[1], out_7[0], Cin, and_1_out, out_7[2]);
  or or_7 (or_7_out, and_8_out, and_13_out);
  or or_8 (or_8_out, and_13_out, and_9_out);
  J_K_Flip_Flop j_k_ff_1 (
    .J(or_1_out), .clk(Clock), .K(or_2_out), .Q(out_7[0]), .reset(Clear));  // open: Qn, preset, en
  J_K_Flip_Flop j_k_ff_2 (
    .J(or_3_out), .clk(Clock), .K(or_4_out), .Q(out_7[1]), .reset(Clear));  // open: Qn, preset, en
  J_K_Flip_Flop j_k_ff_3 (
    .J(or_5_out), .clk(Clock), .K(or_6_out), .Q(out_7[2]), .reset(Clear));  // open: Qn, preset, en
  J_K_Flip_Flop j_k_ff_4 (
    .J(or_7_out), .clk(Clock), .K(or_8_out), .Q(out_7[3]), .reset(Clear));  // open: Qn, preset, en
  and and_14 (Cout, out_7[3], out_7[2], out_7[1], out_7[0], Cin, and_1_out);
  // Probe on out_7

  // Notes on the sheet:
  //   2207111
endmodule

// 1CPL
module _1_Bit_CPL (
  input  Cin,
  input  Count,
  input  Load,
  input  in_4,
  input  Clear,
  input  Clock,
  output out_7
);

  wire and_1_out, and_2_out, and_3_out, and_4_out, not_1_out, not_2_out, or_1_out, or_2_out;

  not not_1 (not_1_out, Load);
  and and_1 (and_1_out, Count, not_1_out);
  not not_2 (not_2_out, in_4);
  and and_2 (and_2_out, Load, in_4);
  and and_3 (and_3_out, Load, not_2_out);
  and and_4 (and_4_out, and_1_out, Cin);
  or or_1 (or_1_out, and_2_out, and_4_out);
  or or_2 (or_2_out, and_4_out, and_3_out);
  J_K_Flip_Flop j_k_ff_1 (.J(or_1_out), .clk(Clock), .K(or_2_out), .Q(out_7), .reset(Clear));  // open: Qn, preset, en

  // Notes on the sheet:
  //   2207111
endmodule

module MBR (
  input  Load,
  input  Count,
  input  [19:0] Input,
  input  Clock,
  input  Clear,
  output [19:0] Output
);

  wire n4_bit_cpl_1_cout, n4_bit_cpl_2_cout, n4_bit_cpl_3_cout, n4_bit_cpl_4_cout, n4_bit_cpl_5_cout;

  _4_Bit_CPL u_4_bit_cpl_1 (
    .Cin(Count), .Count(Count), .Load(Load), .\input (Input[3:0]), .Clock(Clock), .Clear(Clear),
    .out_7(Output[3:0]), .Cout(n4_bit_cpl_1_cout));
  _4_Bit_CPL u_4_bit_cpl_2 (
    .Cin(n4_bit_cpl_1_cout), .Count(Count), .Load(Load), .\input (Input[7:4]), .Clock(Clock), .Clear(Clear),
    .out_7(Output[7:4]), .Cout(n4_bit_cpl_2_cout));
  _4_Bit_CPL u_4_bit_cpl_3 (
    .Cin(n4_bit_cpl_2_cout), .Count(Count), .Load(Load), .\input (Input[11:8]), .Clock(Clock), .Clear(Clear),
    .out_7(Output[11:8]), .Cout(n4_bit_cpl_3_cout));
  _4_Bit_CPL u_4_bit_cpl_4 (
    .Cin(n4_bit_cpl_3_cout), .Count(Count), .Load(Load), .\input (Input[15:12]), .Clock(Clock),
    .Clear(Clear), .out_7(Output[15:12]), .Cout(n4_bit_cpl_4_cout));
  _4_Bit_CPL u_4_bit_cpl_5 (
    .Cin(n4_bit_cpl_4_cout), .Count(Count), .Load(Load), .\input (Input[19:16]), .Clock(Clock),
    .Clear(Clear), .out_7(Output[19:16]), .Cout(n4_bit_cpl_5_cout));
  // Probe on Output

  // Notes on the sheet:
  //   2207111
endmodule

module MAR (
  input  LOAD,
  input  [4:0] Input,
  input  Clock,
  input  Clear,
  output [4:0] out_5
);

  _4_Bit_PLR u_4_bit_plr_1 (.LOAD(LOAD), .in_2(Input[3:0]), .CLOCK(Clock), .CLEAR(Clear), .out_5(out_5[3:0]));
  _1_Bit_PLR u_1_bit_plr_1 (.LOAD(LOAD), .in_2(Input[4]), .CLOCK(Clock), .CLEAR(Clear), .out_5(out_5[4]));

  // Notes on the sheet:
  //   2207111
endmodule

module IR (
  input  Load,
  input  [3:0] Input,
  input  Clock,
  input  Clear,
  output [3:0] IR
);

  wire and_1_out, and_2_out, and_3_out, and_4_out, and_5_out, and_6_out, and_7_out, and_8_out, not_1_out,
       not_2_out, not_3_out, not_4_out;

  not not_1 (not_1_out, Input[0]);
  not not_2 (not_2_out, Input[1]);
  not not_3 (not_3_out, Input[2]);
  not not_4 (not_4_out, Input[3]);
  and and_1 (and_1_out, Input[0], Load);
  and and_2 (and_2_out, not_1_out, Load);
  and and_3 (and_3_out, Input[1], Load);
  and and_4 (and_4_out, not_2_out, Load);
  and and_5 (and_5_out, Input[2], Load);
  and and_6 (and_6_out, not_3_out, Load);
  and and_7 (and_7_out, Input[3], Load);
  and and_8 (and_8_out, not_4_out, Load);
  J_K_Flip_Flop j_k_ff_1 (.J(and_1_out), .clk(Clock), .K(and_2_out), .Q(IR[0]), .reset(Clear));  // open: Qn, preset, en
  J_K_Flip_Flop j_k_ff_2 (.J(and_3_out), .clk(Clock), .K(and_4_out), .Q(IR[1]), .reset(Clear));  // open: Qn, preset, en
  J_K_Flip_Flop j_k_ff_3 (.J(and_5_out), .clk(Clock), .K(and_6_out), .Q(IR[2]), .reset(Clear));  // open: Qn, preset, en
  J_K_Flip_Flop j_k_ff_4 (.J(and_7_out), .clk(Clock), .K(and_8_out), .Q(IR[3]), .reset(Clear));  // open: Qn, preset, en

  // Notes on the sheet:
  //   2207111
endmodule

module PC (
  input  LOAD,
  input  Count,
  input  [4:0] Input,
  input  Clock,
  input  Clear,
  output [4:0] PC
);

  wire n4_bit_cpl_1_cout;

  _4_Bit_CPL u_4_bit_cpl_1 (
    .Cin(Count), .Count(Count), .Load(LOAD), .\input (Input[3:0]), .Clock(Clock), .Clear(Clear),
    .out_7(PC[3:0]), .Cout(n4_bit_cpl_1_cout));
  _1_Bit_CPL u_1_bit_cpl_1 (
    .Cin(n4_bit_cpl_1_cout), .Count(Count), .Load(Input[4]), .in_4(LOAD), .Clear(Clear), .Clock(Clock),
    .out_7(PC[4]));
  // Probe on PC

  // Notes on the sheet:
  //   2207111
endmodule

module AC (
  input  Load,
  input  [19:0] Input,
  input  Clock,
  input  Clear,
  output [19:0] Output
);

  _4_Bit_PLR u_4_bit_plr_1 (.LOAD(Load), .in_2(Input[3:0]), .CLOCK(Clock), .CLEAR(Clear), .out_5(Output[3:0]));
  _4_Bit_PLR u_4_bit_plr_2 (.LOAD(Load), .in_2(Input[7:4]), .CLOCK(Clock), .CLEAR(Clear), .out_5(Output[7:4]));
  _4_Bit_PLR u_4_bit_plr_3 (.LOAD(Load), .in_2(Input[11:8]), .CLOCK(Clock), .CLEAR(Clear), .out_5(Output[11:8]));
  _4_Bit_PLR u_4_bit_plr_4 (.LOAD(Load), .in_2(Input[15:12]), .CLOCK(Clock), .CLEAR(Clear), .out_5(Output[15:12]));
  _4_Bit_PLR u_4_bit_plr_5 (.LOAD(Load), .in_2(Input[19:16]), .CLOCK(Clock), .CLEAR(Clear), .out_5(Output[19:16]));

  // Notes on the sheet:
  //   2207111
endmodule

module REG (
  input  Load,
  input  [3:0] Data_IR,
  input  [19:0] Din,
  input  [4:0] in_4,
  input  Count,
  input  Reset,
  output [19:0] out_7,
  output [3:0] out_8,
  output [4:0] out_9,
  output [19:0] out_10,
  output [4:0] out_11
);

  wire CLK_out;

  Clock CLK (.out(CLK_out));
  MBR mbr_1 (.Load(Load), .Count(Count), .Input(Din), .Clock(CLK_out), .Clear(Reset), .Output(out_7));
  IR ir_1 (.Input(Data_IR), .Clock(CLK_out), .Clear(Reset), .Load(Load), .IR(out_8));
  MAR mar_1 (.LOAD(Load), .Input(in_4), .Clock(CLK_out), .Clear(Reset), .out_5(out_9));
  AC ac_1 (.Load(Load), .Input(Din), .Clock(CLK_out), .Clear(Reset), .Output(out_10));
  PC pc_1 (.LOAD(Load), .Count(Count), .Input(in_4), .Clock(CLK_out), .Clear(Reset), .PC(out_11));
  // Probe on out_7
  // Probe on out_11

  // Notes on the sheet:
  //   2207111 REGISTERS
endmodule

module CU (
  input  clock,
  input  reset,
  input  F,
  input  S,
  input  [3:0] IR,
  input  BZ,
  input  N,
  output ac,
  output bm,
  output c1,
  output ib,
  output f1,
  output cb,
  output ab,
  output f0,
  output sr,
  output bs,
  output mb,
  output b1,
  output ca,
  output bc,
  output sb,
  output ON,
  output shr,
  output xtar,
  output ntar,
  output Ctar
);

  wire and_4_out, and_7_out, and_8_out, and_10_out, and_12_out, and_13_out, and_15_out, and_17_out,
       and_19_out, and_23_out, not_1_out, not_3_out, not_4_out, not_5_out, not_6_out, or_1_out, or_2_out,
       or_5_out, q0, q1, q2, q3, q4, q5, q6, q7, q8, q9, q10, q11, q12, q13, t0, t1, t2, t3;
  wire [1:0] counter_1_q;

  buf or_1 (or_1_out, q1);  // OR_Gate
  Counter #(.width(2), .max('h3)) counter_1 (
    .load(1'b0), .Q(counter_1_q), .clk(clock), .clr(reset));  // open: D, count, carry
  and and_1 (ab, F, t0);
  or or_2 (or_2_out, q10, q11, q0, q1, q7, q2, q3, q9, q12);
  and and_2 (f0, F, t3);
  and and_3 (xtar, F, t2, q9);
  and and_4 (and_4_out, F, t2, q10, not_1_out);
  not not_1 (not_1_out, N);
  and and_5 (ntar, F, t2, q11);
  and and_6 (Ctar, F, t2, q12);
  Decoder #(.select(2)) decoder_1 (.out0(t0), .out1(t1), .out2(t2), .out3(t3), .sel(counter_1_q));  // open: en
  and and_7 (and_7_out, F, q0, t3);
  and and_8 (and_8_out, F, or_1_out, t3);
  and and_9 (bs, F, q2, t2);
  and and_10 (and_10_out, F, q2, t3);
  and and_11 (b1, F, q3, t2);
  and and_12 (and_12_out, F, q3, t3);
  and and_13 (and_13_out, F, q3, BZ, t3);
  and and_14 (bc, F, q4, t2);
  and and_15 (and_15_out, F, q4, t3);
  and and_16 (sb, F, q7, t2);
  and and_17 (and_17_out, q6, t3);
  and and_18 (shr, q8, t3);
  Decoder #(.select(4)) decoder_2 (
    .out0(q0), .out1(q1), .out2(q2), .out3(q3), .out4(q4), .out5(q5), .out6(q6), .out7(q7), .out8(q8),
    .out9(q9), .out10(q10), .out11(q11), .out12(q12), .out13(q13), .sel(IR));  // open: out14, out15, en
  and and_19 (and_19_out, F, or_2_out, t1);
  or or_3 (sr, and_7_out, and_8_out);
  or or_4 (mb, and_10_out, and_15_out, and_12_out);
  not not_2 (ON, and_17_out);
  not not_3 (not_3_out, F);
  not not_4 (not_4_out, F);
  not not_5 (not_5_out, F);
  and and_20 (ib, not_3_out, t2);
  or or_5 (or_5_out, q10, q11, q7, q0, q1, q3, q4, q9, q12, q2);
  and and_21 (cb, q5, t3);
  and and_22 (ac, not_4_out, t0);
  and and_23 (and_23_out, not_5_out, t1);
  not not_6 (not_6_out, F);
  or or_6 (c1, and_23_out, and_13_out, and_15_out, and_4_out);
  and and_24 (f1, not_6_out, or_5_out, t3);
  or or_7 (bm, and_23_out, and_19_out);

  assign ca = bc;

  // Notes on the sheet:
  //   2207111
endmodule

module BZ (
  input  [19:0] in_1,
  output out_2
);

  or or_1 (out_2, in_1[0], in_1[1], in_1[2], in_1[3], in_1[4], in_1[5], in_1[6], in_1[7], in_1[8], in_1[9], in_1[11], in_1[12], in_1[13], in_1[14], in_1[15], in_1[16], in_1[17], in_1[18], in_1[19], in_1[10]);

  // Notes on the sheet:
  //   2207111
endmodule

// Ctrl
module ALU_Control (
  input  [3:0] IR,
  output [1:0] Out
);

  Multiplexer #(.select(4), .width(2)) multiplexer_1 (
    .in0(2'b00), .in1(2'b10), .in2(2'b00), .in3(2'b00), .in4(2'b00), .in5(2'b00), .in6(2'b00), .in7(2'b00),
    .in8(2'b00), .in9(2'b00), .in10(2'b00), .in11(2'b00), .in12(2'b00), .in13(2'b00), .in14(2'b00),
    .in15(2'b00), .out(Out), .sel(IR));  // open: en

  // Notes on the sheet:
  //   2207111
endmodule

module MINI_COMP (
  input  reset
);

  wire ab, ac_t, alu_1_cout, b1, bc, bm, bs, Bz, c1, ca, cb, clock, clock_1_out, Ctar, f0, f1, F_q, ib,
       load_a, load_b, load_c, mb, N, ntra, ON, or_4_out, or_5_out, S, sb, shr, shr_out, sr, xtra;
  wire [1:0] alu_control_1_out, priority_encoder_2_out;
  wire [2:0] priority_encoder_1_out;
  wire [3:0] IR;
  wire [4:0] MAR, multiplexer_1_out, multiplexer_2_out, PC;
  wire [10:0] undriven;
  wire [19:0] AC, Comp, M_out, MBR, multiplexer_3_out, multiplexer_4_out, Nor, result, Xor;

  Clock clock_1 (.out(clock_1_out));
  or or_1 (load_a, ac_t, ab);
  or or_2 (load_c, cb, ca);
  and and_1 (clock, clock_1_out, S);
  Multiplexer #(.width(5)) multiplexer_1 (.in0(MBR[4:0]), .in1(PC), .out(multiplexer_1_out), .sel(ac_t));  // open: en
  Multiplexer #(.width(5)) multiplexer_2 (.in0(MAR), .in1(MBR[4:0]), .out(multiplexer_2_out), .sel(cb));  // open: en
  MAR mar_1 (.LOAD(load_a), .Input(multiplexer_1_out), .Clock(clock), .Clear(reset), .out_5(MAR));
  PC pc_1 (.LOAD(load_c), .Count(c1), .Input(multiplexer_2_out), .Clock(clock), .Clear(reset), .PC(PC));
  Multiplexer #(.select(3), .width(20)) multiplexer_3 (
    .in0(MBR), .in1(result), .in2(Xor), .in3(Comp), .in4(Nor), .out(multiplexer_3_out),
    .sel(priority_encoder_1_out));  // open: in5, in6, in7, en
  Priority_Encoder priority_encoder_1 (
    .in0(sb), .in1(sr), .in2(xtra), .in3(Ctar), .in4(ntra), .out(priority_encoder_1_out));  // open: in5, in6, in7, en_in
  or or_3 (load_b, bc, bs, bm);
  Priority_Encoder #(.select(2)) priority_encoder_2 (
    .in0(bm), .in1(bs), .in2(bc), .out(priority_encoder_2_out));  // open: in3
  or or_4 (or_4_out, sb, sr, xtra, Ctar, ntra);
  Shift shift_1 (
    .load(or_4_out), .Datain(multiplexer_3_out), .Shift(shr), .\input (1'b0), .Clock(clock), .Reset(reset),
    .\output (shr_out), .Dataout(AC));
  MBR mbr_1 (.Load(load_b), .Count(b1), .Input(multiplexer_4_out), .Clock(clock), .Clear(reset), .Output(MBR));
  Multiplexer #(.select(2), .width(20)) multiplexer_4 (
    .in0(M_out), .in1(AC), .in2({4'b0101, undriven, PC}), .out(multiplexer_4_out),
    .sel(priority_encoder_2_out));  // open: in3, en
  IR ir_1 (.Input(MBR[19:16]), .Clock(clock), .Clear(reset), .Load(ib), .IR(IR));
  J_K_Flip_Flop F (.J(f1), .clk(clock), .K(f0), .Q(F_q), .reset(reset));  // open: Qn, preset, en
  // Probe on AC
  // Probe on AC
  BZ bz_1 (.in_1(MBR), .out_2(Bz));
  // Probe on MBR
  ALU_Control alu_control_1 (.IR(IR), .Out(alu_control_1_out));
  _20_Bit_NOR u_20_bit_nor_1 (.in_1(AC), .in_2(MBR), .out_3(Nor));
  CU cu_1 (
    .clock(clock), .reset(reset), .F(F_q), .S(S), .IR(IR), .BZ(Bz), .N(N), .ac(ac_t), .bm(bm), .c1(c1),
    .ib(ib), .f1(f1), .cb(cb), .ab(ab), .f0(f0), .sr(sr), .bs(bs), .mb(mb), .b1(b1), .ca(ca), .bc(bc),
    .sb(sb), .ON(ON), .shr(shr), .xtar(xtra), .ntar(ntra), .Ctar(Ctar));
  D_Flip_Flop u_S (.clk(clock), .D(ON), .Q(S), .reset(reset));  // open: Qn, preset, en
  Alu alu_1 (
    .A(AC), .B(MBR), .C(alu_control_1_out), .Output(result), .COUT(alu_1_cout), .Negative(N));  // open: Overflow, Zero
  or or_5 (or_5_out, alu_1_cout, shr_out);
  RAM #(.addrWidth(5), .dataWidth(20), .bus("separate")) ram_1 (
    .addr(MAR), .din(MBR), .data(M_out), .str(mb), .clk(clock), .ld(bm));  // open: sel, clr
  D_Flip_Flop E (.clk(clock), .D(or_5_out), .reset(reset));  // open: Q, Qn, preset, en
  _20_Bit_XOR u_20_bit_xor_1 (.in_1(AC), .in_2(MBR), .out_3(Xor));
  Complement complement_1 (.in_1(AC), .out_2(Comp));

  // Other names for the same wires on the sheet: MBR_ADR[4:0] = MBR[4:0]; MBR_OP[3:0] = MBR[19:16]

  // Notes on the sheet:
  //   Program Counter
  //   2207111 Tiny 20-bit Computer
  //   Memory Buffer Register
  //   Accumulator Register
  //   Memory Address register
  //   Instruction Register
  //   Fetch Flipflop
  //   NOR
  //   S-register
  //   ALU 20 Bit
  //   RAM
  //   Control Unit
  //   XOR
  //   Complement
  //   INSTRUCTIONS:
  //   0000-AND
  //   0001-ADD
  //   0010-STO
  //   0011-ISZ
  //   0100-BSB
  //   0101-BUN
  //   0110-HLT
  //   0111-LOAD
  //   1000-SHR
  //   1001-XOR
  //   1010-SPA
  //   1011-NOR
  //   1100-CME
endmodule

module _20_Bit_XOR (
  input  [19:0] in_1,
  input  [19:0] in_2,
  output [19:0] out_3
);

  assign out_3 = in_1 ^ in_2;  // XOR_Gate xor_1, 20 bits wide

  // Notes on the sheet:
  //   2207111
endmodule

module Shift (
  input  load,
  input  [19:0] Datain,
  input  Shift,
  input  \input ,
  input  Clock,
  input  Reset,
  output \output ,
  output [19:0] Dataout
);

  wire and_1_out, or_1_out;
  wire [19:0] multiplexer_1_out;

  and and_1 (and_1_out, Shift, Clock);
  or or_1 (or_1_out, load, Shift);
  Multiplexer #(.width(20)) multiplexer_1 (
    .in0(Datain), .in1({\input , Dataout[19:1]}), .out(multiplexer_1_out), .sel(Shift));  // open: en
  D_Flip_Flop d_ff_1 (.clk(and_1_out), .D(Dataout[0]), .Q(\output ));  // open: Qn, preset, en, reset
  AC ac_1 (.Load(or_1_out), .Input(multiplexer_1_out), .Clock(Clock), .Clear(Reset), .Output(Dataout));

  // Notes on the sheet:
  //   2207111
endmodule

module _20_Bit_NOR (
  input  [19:0] in_1,
  input  [19:0] in_2,
  output [19:0] out_3
);

  assign out_3 = ~(in_1 | in_2);  // NOR_Gate nor_1, 20 bits wide

  // Notes on the sheet:
  //   2207111
endmodule

module Complement (
  input  [19:0] in_1,
  output [19:0] out_2
);

  assign out_2 = ~in_1;  // NOT_Gate not_1, 20 bits wide

  // Notes on the sheet:
  //   2207111
endmodule
